# Fritzing sketch Placa_driver_motor (saved by Fritzing 0.9.2b)
perfboards: 1

parts:
  U1 = Optocoupler [package=THT]
  J1 = female pin header, 2 pins [form="♀ (female)"]
  J2 = Screw terminal - 2 pins [package=THT]  # not connected
  R1 = Resistor [tolerance=±5% resistance=220 package=THT]
  J3 = Screw terminal - 2 pins [package=THT]
  R2 = Resistor [tolerance=±5% resistance=1k package=THT]
  R3 = Resistor [tolerance=±5% resistance=680 package=THT]
  R4 = Resistor [tolerance=±5% resistance=10 package=THT]
  Q1 = Basic FET P-Channel [package="TO220 [THT]"]
  D1 = Rectifier Diode [part_number=1N4001 package="300 mil [THT]"]

nets:
  N1: U1.Pin_1, R1.Pin_1
  N2: U1.Pin_2, J1.pin1
  N3: U1.Pin_4, R3.Pin_0
  N4: U1.Pin_5, R2.Pin_0
  N5: J3.pin1, Q1.drain, D1.cathode
  N6: J3.pin2, R3.Pin_1
  N7: R4.Pin_0, Q1.gate
