# Fritzing sketch Placa_temperatura (saved by Fritzing 0.9.2b)
perfboards: 1

parts:
  Q1 = Basic FET N-Channel [package="TO220 [THT]"]
  JP1 = Header 1 [package=1x01_offset]
  JP3 = Header 1 [package=1x01_offset]
  JP4 = Header 1 [package=1x01_offset]
  JP5 = Header 1 [package=1x01_offset]
  J1 = Screw terminal - 2 pins [package=THT]
  J2 = Screw terminal - 2 pins [package=THT]
  R1 = Resistor [tolerance=±5% resistance=100k package=THT]
  R2 = Resistor [tolerance=±5% resistance=10 package=THT]
  U1 = Optocoupler [package=THT]
  R3 = Resistor [tolerance=±5% resistance=680 package=THT]
  R4 = Resistor [tolerance=±5% resistance=1k package=THT]
  R5 = Resistor [tolerance=±5% resistance=220 package=THT]
  R6 = Resistor [tolerance=±5% resistance=6.8k package=THT]
  LED1 = LED - 5mm [color="Red (633nm)" package="5 mm [THT]"]
  IC1 = IC, DIP package, 8 pins [chip_label=LM358]
  R7 = Resistor [tolerance=±5% resistance=270 package=THT]
  JP6 = Header 1 [package=1x01_offset]
  JP7 = Header 1 [package=1x01_offset]
  R8 = Resistor [tolerance=±5% resistance=01k package=THT]  # not connected
  R9 = Resistor [tolerance=±5% resistance=4.7k package=THT]
  R10 = Resistor [tolerance=±5% resistance=1.5k package=THT]

nets:
  N1: Q1.gate, R2.Pin_1
  N2: Q1.drain, J2.pin1, LED1.cathode
  N3: Q1.source, J1.pin1, R1.Pin_1, R3.Pin_0
  N4: JP1.1, IC1.pin1
  N5: JP3.1, R5.Pin_0
  N6: JP4.1, U1.Pin_2, IC1.pin4, R7.Pin_1
  N7: JP5.1, JP6.1
  N8: J1.pin2, J2.pin2, R4.Pin_1
  N9: R1.Pin_0, R2.Pin_0, U1.Pin_4
  N10: U1.Pin_1, R5.Pin_1
  N11: U1.Pin_5, R4.Pin_0
  N12: R6.Pin_1, LED1.anode
  N13: IC1.pin2, R10.Pin_1
  N14: IC1.pin8, R9.Pin_0
  N15: R7.Pin_0, JP7.1

notes:
  5V EDU-CIAA
  GND EDU-CIAA
  PWM
  TEMP
  +24V
  GND
  R_CARTUCHO_1
  R_CARTUCHO_2
